# Fritzing sketch ZoomB1XFourSwitcher (saved by Fritzing 0.9.3b)
circuit board: 7.57863cm x 4.59029cm
breadboards: 1

parts:
  J1 = female pin header, 13 pins [form="♀ (female)"]
  FS1 = female pin header, 1 pin [form="♀ (female)"]
  J4 = female pin header, 14 pins [form="♀ (female)"]
  FS2 = female pin header, 1 pin [form="♀ (female)"]
  J2 = female pin header, 13 pins [form="♀ (female)"]
  R2 = Resistor [tolerance=±5% resistance=1k package=THT]  # not connected
  R3 = Resistor [tolerance=±5% resistance=1k package=THT]  # not connected
  R4 = Resistor [tolerance=±5% resistance=1k package=THT]  # not connected
  R5 = Resistor [tolerance=±5% resistance=1k package=THT]  # not connected
  R6 = Resistor [tolerance=±5% resistance=1k package=THT]  # not connected
  R7 = Resistor [tolerance=±5% resistance=1k package=THT]  # not connected
  R8 = Resistor [tolerance=±5% resistance=1k package=THT]  # not connected
  R9 = Resistor [tolerance=±5% resistance=1k package=THT]  # not connected
  R10 = Resistor [tolerance=±5% resistance=1k package=THT]  # not connected
  R11 = Resistor [tolerance=±5% resistance=1k package=THT]  # not connected
  R12 = Resistor [tolerance=±5% resistance=1k package=THT]  # not connected
  J3 = female pin header, 13 pins [form="♀ (female)"]
  R1 = Resistor [tolerance=±5% resistance=1k package=THT]  # not connected
  J5 = female pin header, 14 pins [form="♀ (female)"]
  R13 = Resistor [tolerance=±5% resistance=1k package=THT]  # not connected
  R14 = Resistor [tolerance=±5% resistance=1k package=THT]  # not connected
  R15 = Resistor [tolerance=±5% resistance=1k package=THT]  # not connected
  R16 = Resistor [tolerance=±5% resistance=1k package=THT]  # not connected
  R17 = Resistor [tolerance=±5% resistance=1k package=THT]  # not connected
  R18 = Resistor [tolerance=±5% resistance=1k package=THT]  # not connected
  R19 = Resistor [tolerance=±5% resistance=1k package=THT]  # not connected
  R20 = Resistor [tolerance=±5% resistance=1k package=THT]  # not connected
  R21 = Resistor [tolerance=±5% resistance=1k package=THT]  # not connected
  R22 = Resistor [tolerance=±5% resistance=1k package=THT]  # not connected
  R23 = Resistor [tolerance=±5% resistance=1k package=THT]  # not connected
  R24 = Resistor [tolerance=±5% resistance=1k package=THT]  # not connected
  R25 = Resistor [tolerance=±5% resistance=1k package=THT]  # not connected
  J6 = female pin header, 14 pins [form="♀ (female)"]
  J7 = female pin header, 14 pins [form="♀ (female)"]

nets:
  N1: J1.pin1, J4.pin1, J2.pin1, J3.pin1, J5.pin1, J6.pin1, J7.pin1, J7.pin2, J7.pin3, J7.pin4, J7.pin5, J7.pin6, J7.pin7, J7.pin8, J7.pin9, J7.pin10, J7.pin11, J7.pin12, J7.pin13, J7.pin14
  N2: J1.pin2, J2.pin2
  N3: J1.pin3, J2.pin3
  N4: J1.pin4, J2.pin4
  N5: J1.pin5, J2.pin5
  N6: J1.pin6, J2.pin6
  N7: J1.pin7, J2.pin7
  N8: J1.pin8, J2.pin8
  N9: J1.pin9, J2.pin9
  N10: J1.pin10, J2.pin10
  N11: J1.pin11, J2.pin11
  N12: J1.pin12, J2.pin12
  N13: J1.pin13, J2.pin13
  N14: FS1.pin1, J4.pin13, J4.pin14, J3.pin13
  N15: J4.pin2, J3.pin2
  N16: J4.pin3, J3.pin3
  N17: J4.pin4, J3.pin4
  N18: J4.pin5, J3.pin5
  N19: J4.pin6, J3.pin6
  N20: J4.pin7, J3.pin7
  N21: J4.pin8, J3.pin8
  N22: J4.pin9, J3.pin9
  N23: J4.pin10, J3.pin10
  N24: J4.pin11, J3.pin11
  N25: J4.pin12, FS2.pin1, J3.pin12

notes:
  tuner
  fs1
  fs2
  fx1
  fx2
  fx3
  fx4
  fx5
  looper
  rhythm
  setting
  mem stomp
  3.3v
  0V
  emit
  base
  col
  GPIO
  V1.0
  Stephen Hookings
  ZOOM B1XFour Control
  Zoom
  footswitch
